// Logisim project Trial By Fire.003.00.circ as structural Verilog: 1 circuit, main circuit main
module main (
  input  x,
  input  y,
  input  z,
  output out_4
);

  wire not_1_out, not_2_out, x_prime_yz_out, x_prime_yz_prime_out, xyz_out;

  not not_1 (not_1_out, x);
  not not_2 (not_2_out, z);
  and xyz (xyz_out, x, y, z);
  // AND_Gate xyz_prime has open pins: in0=x, in1=y, in2=not_2_out, out=open
  and x_prime_yz (x_prime_yz_out, not_1_out, y, z);
  and x_prime_yz_prime (x_prime_yz_prime_out, not_1_out, y, not_2_out);
  or or_1 (out_4, xyz_out, x_prime_yz_out, y, x_prime_yz_prime_out);
endmodule
