// Logisim project Trial By Fire.003.02.circ as structural Verilog: 1 circuit, main circuit main
module main (
  input  x,
  input  y,
  input  z,
  output out_4
);

  wire not_1_out, not_2_out, or_1_out, xz_out, xz_prime_out, yz_out;

  and xz (xz_out, x, z);
  not not_1 (not_1_out, x);
  and xz_prime (xz_prime_out, x, not_2_out);
  not not_2 (not_2_out, z);
  and yz (yz_out, y, z);
  or or_1 (or_1_out, xz_out, not_1_out, xz_prime_out);
  and and_1 (out_4, or_1_out, yz_out);

  // Notes on the sheet:
  //   (xz + x ' + xz ')
  //   yz(xz + x’ + xz’)
endmodule
